# Fritzing sketch FinalFritzDiagram (saved by Fritzing 1.0.1rc)
breadboards: 1

parts:
  Part1 = Arduino Uno (Rev3) - ICSP
  S1 = Pushbutton [package="[THT]"]
  U1 = WS2812 RGB LED strip
  R1 = Resistor [tolerance=±5% resistance=220 package="2512 [SMD]"]

nets:
  N1: Part1.D2, S1.Pin_3, S1.Pin_4
  N2: Part1.D3_PWM, R1.Pin_1
  5V: Part1.5V, U1.VCC
  GND: Part1.GND, S1.Pin_1, S1.Pin_2, U1.GND
  N3: U1.DIN, R1.Pin_0

custom parts:
  WS2812 RGB LED strip: WS2812 strip
