# Fritzing sketch FinalFritzDiagramV0 (saved by Fritzing 1.0.1rc)
breadboards: 1

parts:
  Part1 = Arduino Uno (Rev3) - ICSP
  S1 = Pushbutton [package="[THT]"]
  U1 = WS2812 RGB LED strip
  R1 = Resistor [tolerance=±5% resistance=220 package="2512 [SMD]"]
  Part2 = Triple Axis Accelerometer Breakout - ADXL345
  Mod1 = KY-023 Dual Axis Joystick Module [package="Breakout board"]

nets:
  N1: Part1.A0, Mod1.VRx
  N2: Part1.A1, Mod1.VRy
  N3: Part1.A4/SDA, Part2.SDA
  N4: Part1.A5/SCL, Part2.SCL
  N5: Part1.D2, S1.Pin_3, S1.Pin_4
  N6: Part1.D3_PWM, R1.Pin_1
  N7: Part1.D4, Mod1.SW
  VCC: Part1.5V, U1.VCC, Part2.VCC, Mod1.+5V
  GND: Part1.GND, S1.Pin_1, S1.Pin_2, U1.GND, Part2.GND, Mod1.GND
  N8: U1.DIN, R1.Pin_0

notes:
  Accelerometer
  LED Strip

custom parts:
  WS2812 RGB LED strip: WS2812 strip
  KY-023 Dual Axis Joystick Module: KY-023 Dual-Axis Joystick Module.
