# Fritzing sketch FinalFritzDiagramV1 (saved by Fritzing 1.0.1rc)
circuit board: 8.46667cm x 5.64444cm
breadboards: 1

parts:
  S1 = Pushbutton [package="[THT]"]  # not connected
  U1 = WS2812 RGB LED strip
  R1 = Resistor [tolerance=±5% resistance=220 package="2512 [SMD]"]
  Part2 = Triple Axis Accelerometer Breakout - ADXL345
  Mod1 = KY-023 Dual Axis Joystick Module [package="Breakout board"]
  Mod2 = KY-023 Dual Axis Joystick Module [package="Breakout board"]
  R2 = Resistor [tolerance=±5% resistance=220 package="2512 [SMD]"]
  LED1 = LED - 5mm [color="Red (633nm)" current=0.030A package="5 mm [THT]"]
  LED2 = LED - 5mm [color="Red (633nm)" current=0.030A package="5 mm [THT]"]
  LED3 = LED - 5mm [color="Red (633nm)" current=0.030A package="5 mm [THT]"]
  LED4 = LED - 5mm [color="Red (633nm)" current=0.030A package="5 mm [THT]"]
  R3 = Resistor [tolerance=±5% resistance=220 package="2512 [SMD]"]
  R4 = Resistor [tolerance=±5% resistance=220 package="2512 [SMD]"]
  R5 = Resistor [tolerance=±5% resistance=220 package="2512 [SMD]"]
  Part3 = Arduino Uno (Rev3) - ICSP

nets:
  GND: U1.GND, Part2.GND, Mod1.GND, Mod2.GND, LED1.cathode, LED2.cathode, LED3.cathode, LED4.cathode, Part3.GND
  VCC: U1.VCC, Part2.VCC, Mod1.+5V, Mod2.+5V, R2.Pin_0, R3.Pin_0, R4.Pin_0, R5.Pin_0, Part3.5V
  N1: U1.DOUT, R1.Pin_0
  N2: R1.Pin_1, Part3.D13/SCK
  N3: Part2.SDA, Mod2.VRx, Part3.A4/SDA
  N4: Part2.SCL, Mod2.VRy, Part3.A5/SCL
  N5: Mod1.VRx, Part3.A2
  N6: Mod1.VRy, Part3.A3
  N7: Mod1.SW, Part3.D3_PWM
  N8: Mod2.SW, Part3.D2
  N9: R2.Pin_1, LED1.anode
  N10: LED2.anode, R5.Pin_1
  N11: LED3.anode, R4.Pin_1
  N12: LED4.anode, R3.Pin_1

notes:
  Trigger Switch for LEDS
  Accelerometer/Gyro
  Dual Analog Sticks
  Passive power LEDs
  LED Strip

custom parts:
  WS2812 RGB LED strip: WS2812 strip
  KY-023 Dual Axis Joystick Module: KY-023 Dual-Axis Joystick Module.
