# Fritzing sketch FinalFritzDiagramV2 (saved by Fritzing 1.0.1rc)
breadboards: 2

parts:
  S1 = Pushbutton [package="[THT]"]
  U1 = WS2812 RGB LED strip
  Mod1 = KY-023 Dual Axis Joystick Module [package="Breakout board"]
  Mod2 = KY-023 Dual Axis Joystick Module [package="Breakout board"]
  LED1 = LED - 5mm [color="Red (633nm)" current=0.030A package="5 mm [THT]"]  # not connected
  LED2 = LED - 5mm [color="Red (633nm)" current=0.030A package="5 mm [THT]"]  # not connected
  LED3 = LED - 5mm [color="Red (633nm)" current=0.030A package="5 mm [THT]"]  # not connected
  LED4 = LED - 5mm [color="Red (633nm)" current=0.030A package="5 mm [THT]"]  # not connected
  R3 = Resistor [tolerance=±5% resistance=220 package="2512 [SMD]"]  # not connected
  R4 = Resistor [tolerance=±5% resistance=220 package="2512 [SMD]"]  # not connected
  R5 = Resistor [tolerance=±5% resistance=220 package="2512 [SMD]"]  # not connected
  R6 = Resistor [tolerance=±5% resistance=220 package="2512 [SMD]"]  # not connected
  Part3 = Arduino Uno (Rev3) - ICSP
  R7 = Resistor [tolerance=±5% resistance=220 package="2512 [SMD]"]
  Part4 = Adafruit BNO085 9-DOF Orientation IMU Fusion [part_number="Addfruit #4754"]  # not connected
  Part5 = Adafruit HUZZAH32 ESP32 Feather [part_number="Adafruit #3405"]  # not connected

nets:
  N1: S1.Pin_1, S1.Pin_2, Part3.ICSP_MISO, Part3.D12/MISO
  GND: S1.Pin_3, S1.Pin_4, U1.GND, Mod1.GND, Mod2.GND, Part3.GND
  +5V: U1.VCC, Mod1.+5V, Mod2.+5V, Part3.5V
  N2: U1.DOUT, R7.Pin_0
  N3: Part3.D13/SCK, R7.Pin_1

notes:
  Power Board
  Control Board

custom parts:
  WS2812 RGB LED strip: WS2812 strip
  KY-023 Dual Axis Joystick Module: KY-023 Dual-Axis Joystick Module.
