# Fritzing sketch FinalFritzDiagramV3 (saved by Fritzing 1.0.1rc)
breadboards: 2

parts:
  U1 = WS2812 RGB LED strip
  Mod1 = KY-023 Dual Axis Joystick Module [package="Breakout board"]
  Mod2 = KY-023 Dual Axis Joystick Module [package="Breakout board"]
  LED1 = LED - 5mm [color="Red (633nm)" current=0.030A package="5 mm [THT]"]
  LED2 = LED - 5mm [color="Red (633nm)" current=0.030A package="5 mm [THT]"]
  LED3 = LED - 5mm [color="Red (633nm)" current=0.030A package="5 mm [THT]"]
  LED4 = LED - 5mm [color="Red (633nm)" current=0.030A package="5 mm [THT]"]
  R3 = Resistor [tolerance=±5% resistance=220 package="2512 [SMD]"]
  R4 = Resistor [tolerance=±5% resistance=220 package="2512 [SMD]"]
  R5 = Resistor [tolerance=±5% resistance=220 package="2512 [SMD]"]
  R6 = Resistor [tolerance=±5% resistance=220 package="2512 [SMD]"]
  R7 = Resistor [tolerance=±5% resistance=220 package="2512 [SMD]"]
  Part4 = Adafruit BNO085 9-DOF Orientation IMU Fusion [part_number="Addfruit #4754"]  # not connected
  Part5 = Adafruit HUZZAH32 ESP32 Feather [part_number="Adafruit #3405"]
  S1 = Pushbutton [package="[THT]"]
  Part6 = Arduino Uno (Rev3) - ICSP

nets:
  GND: U1.GND, Mod1.GND, Mod2.GND, LED1.cathode, LED2.cathode, LED3.cathode, LED4.cathode, Part5.GND, S1.Pin_1, S1.Pin_2, Part6.GND
  +5V: U1.VCC, Mod1.+5V, Mod2.+5V, R3.Pin_0, R4.Pin_0, R5.Pin_0, R6.Pin_0, Part5.3.3V, Part6.5V
  N1: U1.DOUT, R7.Pin_0
  N2: Mod1.VRx, Part6.A0
  N3: Mod1.VRy, Part6.A1
  N4: Mod1.SW, Part6.D4
  N5: Mod2.VRx, Part6.A2
  N6: Mod2.VRy, Part6.A3
  N7: Mod2.SW, Part6.D5_PWM
  N8: LED1.anode, R3.Pin_1
  N9: LED2.anode, R5.Pin_1
  N10: LED3.anode, R6.Pin_1
  N11: LED4.anode, R4.Pin_1
  N12: R7.Pin_1, Part6.D3_PWM
  N13: S1.Pin_4, Part6.D2

custom parts:
  WS2812 RGB LED strip: WS2812 strip
  KY-023 Dual Axis Joystick Module: KY-023 Dual-Axis Joystick Module.
