# Fritzing sketch FinalFritzDiagramV4 (saved by Fritzing 1.0.1rc)
breadboards: 2

parts:
  U1 = WS2812 RGB LED strip
  Mod1 = KY-023 Dual Axis Joystick Module [package="Breakout board"]
  Mod2 = KY-023 Dual Axis Joystick Module [package="Breakout board"]
  LED1 = LED - 5mm [color="Red (633nm)" current=0.030A package="5 mm [THT]"]
  LED2 = LED - 5mm [color="Red (633nm)" current=0.030A package="5 mm [THT]"]
  LED4 = LED - 5mm [color="Red (633nm)" current=0.030A package="5 mm [THT]"]
  R5 = Resistor [tolerance=±5% resistance=220 package="2512 [SMD]"]
  R7 = Resistor [tolerance=±5% resistance=220 package="2512 [SMD]"]
  Part4 = Adafruit BNO085 9-DOF Orientation IMU Fusion [part_number="Addfruit #4754"]
  Part5 = Adafruit HUZZAH32 ESP32 Feather [part_number="Adafruit #3405"]
  S1 = Pushbutton [package="[THT]"]
  R8 = Resistor [tolerance=±5% resistance=220 package="2010 [SMD]"]
  R9 = Resistor [tolerance=±5% resistance=220 package="2512 [SMD]"]
  LED5 = LED - 5mm [color="Red (633nm)" current=0.030A package="5 mm [THT]"]
  R10 = Resistor [tolerance=±5% resistance=220 package="2512 [SMD]"]

nets:
  GND: U1.GND, Mod1.GND, Mod2.GND, LED1.cathode, LED2.cathode, LED4.cathode, Part4.GND, Part5.GND, S1.Pin_1, S1.Pin_2, LED5.cathode
  VCC: U1.VCC, Mod1.+5V, Mod2.+5V, R5.Pin_1, Part4.VCC, Part5.VBAT, R8.Pin_1, R9.Pin_1, R10.Pin_1
  N1: U1.DOUT, R7.Pin_0
  N2: LED1.anode, R8.Pin_0
  N3: LED2.anode, R9.Pin_0
  N4: LED4.anode, R5.Pin_0
  N5: LED5.anode, R10.Pin_0

custom parts:
  WS2812 RGB LED strip: WS2812 strip
  KY-023 Dual Axis Joystick Module: KY-023 Dual-Axis Joystick Module.
