# Fritzing sketch FinalFritzDiagramV5 (saved by Fritzing 1.0.1rc)
breadboards: 1

parts:
  U1 = WS2812 RGB LED strip
  Mod1 = KY-023 Dual Axis Joystick Module [package="Breakout board"]
  Mod2 = KY-023 Dual Axis Joystick Module [package="Breakout board"]
  LED1 = LED - 5mm [color="Red (633nm)" current=0.030A package="5 mm [THT]"]
  LED2 = LED - 5mm [color="Red (633nm)" current=0.030A package="5 mm [THT]"]
  LED4 = LED - 5mm [color="Red (633nm)" current=0.030A package="5 mm [THT]"]
  R5 = Resistor [tolerance=±5% resistance=220 package="2512 [SMD]"]
  R7 = Resistor [tolerance=±5% resistance=220 package="2512 [SMD]"]
  S1 = Pushbutton [package="[THT]"]
  R8 = Resistor [tolerance=±5% resistance=220 package="2010 [SMD]"]
  R9 = Resistor [tolerance=±5% resistance=220 package="2512 [SMD]"]
  LED5 = LED - 5mm [color="Red (633nm)" current=0.030A package="5 mm [THT]"]
  R10 = Resistor [tolerance=±5% resistance=220 package="2512 [SMD]"]
  Part7 = Arduino MKR WIFI 1010
  Part8 = 9DOF Sensor LSM9DS0

nets:
  GND: U1.GND, Mod1.GND, Mod2.GND, LED1.cathode, LED2.cathode, LED4.cathode, S1.Pin_1, S1.Pin_2, LED5.cathode, Part7.GND, Part8.GND
  +5V: U1.VCC, Mod1.+5V, Mod2.+5V, R5.Pin_0, R7.Pin_0, R9.Pin_0, R10.Pin_0, Part7.5V, Part8.VDD
  N1: U1.DIN, R8.Pin_1
  N2: Mod1.VRx, Part7.A3
  N3: Mod1.VRy, Part7.A2
  N4: Mod1.SW, Part7.D2_PWM
  N5: Mod2.VRx, Part7.DAC0/A0
  N6: Mod2.VRy, Part7.A1
  N7: Mod2.SW, Part7.D1
  N8: LED1.anode, R5.Pin_1
  N9: LED2.anode, R10.Pin_1
  N10: LED4.anode, R9.Pin_1
  N11: S1.Pin_4, Part7.D3_PWM
  N12: R8.Pin_0, Part7.D4_PWM
  N13: Part7.D8/MOSI, Part8.DRDYG
  N14: Part7.D9/SCK, Part8.INTG
  N15: Part7.D11/SDA, Part8.SDA
  N16: Part7.D12/SCL, Part8.SCL
  N17: Part7.D6, Part8.INT2XM
  N18: Part7.D7, Part8.INT1XM

notes:
  Data ports:
  A0 - Joystick A X
  A1 - Joystick A Y
  A2 - Joystick B X
  A3 - Joystick B Y
  1 - Joystick A Select
  2 - Joystick B Select
  3 - Button
  4 - Smart LEDs
  SCL - 9DOF SCL
  SDA - 9DOF SDA
  9 - 9DOF INTG
  8 - 9DOF DRYDYG
  7 - 9DOF INT1XM
  6 - 9DOF INT2XM

custom parts:
  WS2812 RGB LED strip: WS2812 strip
  KY-023 Dual Axis Joystick Module: KY-023 Dual-Axis Joystick Module.
  Arduino MKR WIFI 1010: The MKR WIFI 1010 is a significant improvement on the MKR 1000 WIFI. It's equipped with an ESP32 module made by U-BLOX. This board aims to speed up and simplify the prototyping of WiFi based IoT applications thanks to the flexibility of the ESP32 module and its low power consumption. The board is composed of three main blocks: SAMD21 Cortex-M0+ 32bit Low Power ARM MCU; U-BLOX NINA-W10 Series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
  9DOF Sensor LSM9DS0: This is the LSM9DS0, a versatile motion-sensing system-in-a-chip that houses a 3-axis accelerometer, 3-axis gyroscope, and 3-axis magnetometer. That’s right, 9 degrees of freedom (9dof) from a single IC! Each sensor in the LSM9DS0 supports a wide range of, well, ranges: the accelerometer’s scale can be set to ± 2, 4, 6, 8, or 16 g, the gyroscope supports ± 245, 500, and 2000 °/s, and the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
