# Fritzing sketch FinalFritzDiagramV7 (saved by Fritzing 1.0.1rc)
breadboards: 1

parts:
  U1 = WS2812 RGB LED strip
  LED1 = LED - 5mm [color="Red (633nm)" current=0.030A package="5 mm [THT]"]
  LED2 = LED - 5mm [color="Red (633nm)" current=0.030A package="5 mm [THT]"]
  LED4 = LED - 5mm [color="Red (633nm)" current=0.030A package="5 mm [THT]"]
  R5 = Resistor [tolerance=±5% resistance=220 package="2512 [SMD]"]
  R7 = Resistor [tolerance=±5% resistance=220 package="2512 [SMD]"]
  S1 = Pushbutton [package="[THT]"]
  R8 = Resistor [tolerance=±5% resistance=220 package="2010 [SMD]"]
  R9 = Resistor [tolerance=±5% resistance=220 package="2512 [SMD]"]
  LED5 = LED - 5mm [color="Red (633nm)" current=0.030A package="5 mm [THT]"]
  R10 = Resistor [tolerance=±5% resistance=220 package="2512 [SMD]"]
  Part7 = Arduino MKR WIFI 1010
  Part8 = Adafruit BNO085 9-DOF Orientation IMU Fusion [part_number="Addfruit #4754"]
  R11 = Resistor [tolerance=±5% resistance=3.3k package="2512 [SMD]"]

nets:
  GND: U1.GND, LED1.cathode, LED2.cathode, LED4.cathode, S1.Pin_1, S1.Pin_2, LED5.cathode, Part7.GND, Part8.GND
  VCC: U1.VCC, R5.Pin_0, R7.Pin_0, R9.Pin_0, R10.Pin_0, Part7.5V
  N1: U1.DIN, R8.Pin_1
  N2: LED1.anode, R5.Pin_1
  N3: LED2.anode, R10.Pin_1
  N4: LED4.anode, R9.Pin_1
  N5: S1.Pin_4, Part7.D3_PWM
  N6: R8.Pin_0, Part7.D4_PWM
  N7: Part7.D11/SDA, R11.Pin_0
  N8: Part7.D12/SCL, Part8.SCL/SCK/RX
  VCC_2: Part7.VCC, Part8.VCC
  N9: Part8.SDA/MISO/TX, R11.Pin_1

notes:
  Data ports:
  A0 - Joystick A X
  A1 - Joystick A Y
  A2 - Joystick B X
  A3 - Joystick B Y
  1 - Joystick A Select
  2 - Joystick B Select
  3 - Button
  4 - Smart LEDs
  SCL - 9DOF SCL
  SDA - 9DOF SDA

custom parts:
  WS2812 RGB LED strip: WS2812 strip
  Arduino MKR WIFI 1010: The MKR WIFI 1010 is a significant improvement on the MKR 1000 WIFI. It's equipped with an ESP32 module made by U-BLOX. This board aims to speed up and simplify the prototyping of WiFi based IoT applications thanks to the flexibility of the ESP32 module and its low power consumption. The board is composed of three main blocks: SAMD21 Cortex-M0+ 32bit Low Power ARM MCU; U-BLOX NINA-W10 Series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
