# Fritzing sketch FinalFritzDiagramV8 (saved by Fritzing 1.0.1rc)
breadboards: 1

parts:
  U1 = WS2812 RGB LED strip
  LED1 = LED - 5mm [color="Red (633nm)" current=0.030A package="5 mm [THT]"]
  LED2 = LED - 5mm [color="Red (633nm)" current=0.030A package="5 mm [THT]"]
  LED4 = LED - 5mm [color="Red (633nm)" current=0.030A package="5 mm [THT]"]
  R5 = Resistor [tolerance=±5% resistance=220 package="2512 [SMD]"]
  R7 = Resistor [tolerance=±5% resistance=220 package="2512 [SMD]"]
  S1 = Pushbutton [package="[THT]"]
  R8 = Resistor [tolerance=±5% resistance=220 package="2010 [SMD]"]
  R9 = Resistor [tolerance=±5% resistance=220 package="2512 [SMD]"]
  LED5 = LED - 5mm [color="Red (633nm)" current=0.030A package="5 mm [THT]"]
  R10 = Resistor [tolerance=±5% resistance=220 package="2512 [SMD]"]
  R11 = Resistor [tolerance=±5% resistance=3.3k package="2512 [SMD]"]  # not connected
  Part1 = Adafruit HUZZAH32 ESP32 Feather [part_number="Adafruit #3405"]  # not connected
  Part2 = 9DOF Sensor LSM9DS0  # not connected

nets:
  N1: U1.GND, LED1.cathode, LED2.cathode, LED4.cathode, S1.Pin_1, S1.Pin_2, LED5.cathode
  N2: U1.VCC, R5.Pin_0, R7.Pin_0, R9.Pin_0, R10.Pin_0
  N3: U1.DIN, R8.Pin_1
  N4: LED1.anode, R5.Pin_1
  N5: LED2.anode, R10.Pin_1
  N6: LED4.anode, R9.Pin_1

notes:
  Data ports:
  DOF SCL - SCL
  DOF SDA - SDA
  LED Pin -
  Button Pin -
  INT1XM -

custom parts:
  WS2812 RGB LED strip: WS2812 strip
  9DOF Sensor LSM9DS0: This is the LSM9DS0, a versatile motion-sensing system-in-a-chip that houses a 3-axis accelerometer, 3-axis gyroscope, and 3-axis magnetometer. That’s right, 9 degrees of freedom (9dof) from a single IC! Each sensor in the LSM9DS0 supports a wide range of, well, ranges: the accelerometer’s scale can be set to ± 2, 4, 6, 8, or 16 g, the gyroscope supports ± 245, 500, and 2000 °/s, and the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
